// Logisim project digital watch.circ as structural Verilog: 10 circuits, main circuit main
module main (
);

  wire a_out, ab_out, b_out, button_converter_1_s, button_converter_1_x1, button_converter_1_x2, gen, i1, i2,
       i3, L1, L2, L3, L4, L5, L6, signal_1_signal;
  wire [3:0] hours_tens, hours_units, minutes_tens, minutes_units, sec_tens, sec_units, SW_minutes_tens,
       SW_minutes_units, SW_sec_tens, SW_sec_units;
  wire [6:0] controlled_buffer_1_out, controlled_buffer_2_out, controlled_buffer_5_out,
       controlled_buffer_6_out, indicator_converter_1_output, indicator_converter_2_output,
       indicator_converter_3_output, indicator_converter_4_output, indicator_converter_5_output,
       indicator_converter_6_output, indicator_converter_7_output, indicator_converter_8_output;

  Button a (.out(a_out));
  Button b (.out(b_out));
  Button ab (.out(ab_out));
  button_converter button_converter_1 (
    .a(a_out), .b(b_out), .ab(ab_out), .s(button_converter_1_s), .x1(button_converter_1_x1),
    .x2(button_converter_1_x2));
  assign controlled_buffer_1_out = L4 ? indicator_converter_1_output : 7'bz;  // Controlled_Buffer controlled_buffer_1
  indicator_converter indicator_converter_1 (.\input (SW_minutes_tens), .\output (indicator_converter_1_output));
  assign controlled_buffer_2_out = L4 ? indicator_converter_2_output : 7'bz;  // Controlled_Buffer controlled_buffer_2
  indicator_converter indicator_converter_2 (.\input (SW_minutes_units), .\output (indicator_converter_2_output));
  state_machine state_machine_1 (
    .s(button_converter_1_s), .x1(button_converter_1_x1), .x2(button_converter_1_x2), .L1(L1), .L2(L2),
    .L3(L3), .L4(L4), .L5(L5), .L6(L6), .i1(i1), .i2(i2), .i3(i3));
  assign controlled_buffer_1_out = L2 ? indicator_converter_3_output : 7'bz;  // Controlled_Buffer controlled_buffer_3
  indicator_converter indicator_converter_3 (.\input (hours_tens), .\output (indicator_converter_3_output));
  _7_Segment_Display u_7_segment_display_1 (
    .g(controlled_buffer_1_out[6]), .f(controlled_buffer_1_out[5]), .a(controlled_buffer_1_out[4]),
    .b(controlled_buffer_1_out[3]), .e(controlled_buffer_1_out[0]), .d(controlled_buffer_1_out[1]),
    .c(controlled_buffer_1_out[2]));  // open: dp
  _7_Segment_Display u_7_segment_display_2 (
    .g(controlled_buffer_2_out[6]), .f(controlled_buffer_2_out[5]), .a(controlled_buffer_2_out[4]),
    .b(controlled_buffer_2_out[3]), .e(controlled_buffer_2_out[0]), .d(controlled_buffer_2_out[1]),
    .c(controlled_buffer_2_out[2]));  // open: dp
  assign controlled_buffer_2_out = L2 ? indicator_converter_4_output : 7'bz;  // Controlled_Buffer controlled_buffer_4
  indicator_converter indicator_converter_4 (.\input (hours_units), .\output (indicator_converter_4_output));
  Clock clock_1 (.out(gen));
  _7_Segment_Display u_7_segment_display_3 (
    .g(controlled_buffer_5_out[6]), .f(controlled_buffer_5_out[5]), .a(controlled_buffer_5_out[4]),
    .b(controlled_buffer_5_out[3]), .e(controlled_buffer_5_out[0]), .d(controlled_buffer_5_out[1]),
    .c(controlled_buffer_5_out[2]));  // open: dp
  assign controlled_buffer_5_out = L1 ? indicator_converter_5_output : 7'bz;  // Controlled_Buffer controlled_buffer_5
  indicator_converter indicator_converter_5 (.\input (minutes_tens), .\output (indicator_converter_5_output));
  _7_Segment_Display u_7_segment_display_4 (
    .g(controlled_buffer_6_out[6]), .f(controlled_buffer_6_out[5]), .a(controlled_buffer_6_out[4]),
    .b(controlled_buffer_6_out[3]), .e(controlled_buffer_6_out[0]), .d(controlled_buffer_6_out[1]),
    .c(controlled_buffer_6_out[2]));  // open: dp
  assign controlled_buffer_6_out = L1 ? indicator_converter_6_output : 7'bz;  // Controlled_Buffer controlled_buffer_6
  indicator_converter indicator_converter_6 (.\input (minutes_units), .\output (indicator_converter_6_output));
  clock clock_2 (
    .generator(gen), .i1_signal(i1), .i2_signal(i2), .hours_tens(hours_tens), .hours_units(hours_units),
    .minutes_tens(minutes_tens), .minutes_units(minutes_units), .sec_tens(sec_tens), .sec_units(sec_units),
    .L5(L5), .L6(L6));
  assign controlled_buffer_5_out = L3 ? indicator_converter_7_output : 7'bz;  // Controlled_Buffer controlled_buffer_7
  indicator_converter indicator_converter_7 (.\input (SW_sec_tens), .\output (indicator_converter_7_output));
  LED led_1 (.in(signal_1_signal));
  assign controlled_buffer_6_out = L3 ? indicator_converter_8_output : 7'bz;  // Controlled_Buffer controlled_buffer_8
  indicator_converter indicator_converter_8 (.\input (SW_sec_units), .\output (indicator_converter_8_output));
  signal signal_1 (.in_3(gen), .tens(minutes_tens), .units(minutes_units), .signal(signal_1_signal));
  stop_watch stop_watch_1 (
    .generator(gen), .i3_signal(i3), .minutes_tens(SW_minutes_tens), .minutes_units(SW_minutes_units),
    .sec_tens(SW_sec_tens), .sec_units(SW_sec_units), .L5(L5), .L6(L6));
endmodule

// I.C.
module indicator_converter (
  input  [3:0] \input ,
  output [6:0] \output 
);

  wire and_1_out, and_2_out, and_3_out, and_4_out, and_5_out, and_6_out, and_7_out, and_8_out, and_9_out,
       and_10_out, and_11_out, and_12_out, and_13_out, and_14_out, and_15_out, and_16_out, and_17_out,
       and_18_out, and_19_out, and_20_out, and_21_out, and_22_out, and_23_out, and_24_out, and_25_out,
       and_26_out;

  and and_1 (and_1_out, \input [3], ~\input [2], ~\input [1]);  // AND_Gate
  and and_2 (and_2_out, ~\input [3], \input [2], ~\input [1]);  // AND_Gate
  and and_3 (and_3_out, ~\input [3], \input [1], ~\input [0]);  // AND_Gate
  and and_4 (and_4_out, ~\input [3], ~\input [2], \input [1]);  // AND_Gate
  and and_5 (and_5_out, \input [3], ~\input [2], ~\input [1]);  // AND_Gate
  and and_6 (and_6_out, ~\input [3], \input [2], ~\input [0]);  // AND_Gate
  and and_7 (and_7_out, ~\input [3], \input [2], ~\input [1]);  // AND_Gate
  and and_8 (and_8_out, ~\input [2], ~\input [1], ~\input [0]);  // AND_Gate
  and and_9 (and_9_out, ~\input [3], \input [1]);  // AND_Gate
  and and_10 (and_10_out, ~\input [3], \input [2], \input [0]);  // AND_Gate
  and and_11 (and_11_out, ~\input [2], ~\input [1], ~\input [0]);  // AND_Gate
  and and_12 (and_12_out, \input [3], ~\input [2], ~\input [1]);  // AND_Gate
  and and_13 (and_13_out, ~\input [2], ~\input [1]);  // AND_Gate
  and and_14 (and_14_out, ~\input [3], \input [1], \input [0]);  // AND_Gate
  and and_15 (and_15_out, ~\input [3], ~\input [2]);  // AND_Gate
  and and_16 (and_16_out, ~\input [3], ~\input [1], ~\input [0]);  // AND_Gate
  and and_17 (and_17_out, ~\input [3], \input [2]);  // AND_Gate
  and and_18 (and_18_out, ~\input [3], \input [0]);  // AND_Gate
  and and_19 (and_19_out, ~\input [2], ~\input [1]);  // AND_Gate
  and and_20 (and_20_out, ~\input [3], \input [1], ~\input [0]);  // AND_Gate
  and and_21 (and_21_out, ~\input [3], ~\input [2], \input [1]);  // AND_Gate
  and and_22 (and_22_out, ~\input [2], ~\input [1], ~\input [0]);  // AND_Gate
  and and_23 (and_23_out, ~\input [3], \input [2], ~\input [1], \input [0]);  // AND_Gate
  and and_24 (and_24_out, \input [3], ~\input [2], ~\input [1]);  // AND_Gate
  and and_25 (and_25_out, ~\input [3], \input [1], ~\input [0]);  // AND_Gate
  and and_26 (and_26_out, ~\input [2], ~\input [1], ~\input [0]);  // AND_Gate
  or f0 (\output [6], and_1_out, and_2_out, and_3_out, and_4_out);
  or f1 (\output [5], and_5_out, and_6_out, and_7_out, and_8_out);
  or f2 (\output [4], and_9_out, and_10_out, and_11_out, and_12_out);
  or f3 (\output [3], and_13_out, and_14_out, and_15_out, and_16_out);
  or f4 (\output [2], and_17_out, and_18_out, and_19_out);
  or f5 (\output [1], and_20_out, and_21_out, and_22_out, and_23_out, and_24_out);
  or f6 (\output [0], and_25_out, and_26_out);
  _7_Segment_Display u_7_segment_display_1 (
    .g(\output [6]), .f(\output [5]), .a(\output [4]), .b(\output [3]), .e(\output [0]), .d(\output [1]),
    .c(\output [2]));  // open: dp

  // Notes on the sheet:
  //   x0
  //   x0
  //   x1
  //   x2
  //   x3
  //   x1
  //   x2
  //   x3
endmodule

module F (
  input  x1,
  input  x2,
  input  q1,
  input  q2,
  input  q3,
  output i1,
  output i2,
  output i3,
  output Q1_2,
  output Q2_2,
  output Q3_2
);

  wire and_1_out, and_2_out, and_3_out, and_4_out, and_5_out, and_6_out, and_7_out, and_8_out, and_9_out,
       and_10_out, and_11_out, and_12_out, and_13_out;

  and and_1 (and_1_out, x1, ~q2, ~q3);  // AND_Gate
  and and_2 (and_2_out, ~x2, q1, ~q2);  // AND_Gate
  and and_3 (and_3_out, ~x1, q1, q2);  // AND_Gate
  and and_4 (and_4_out, x2, ~q1, ~q2, ~q3);  // AND_Gate
  and and_5 (and_5_out, x1, ~q1, q2);  // AND_Gate
  and and_6 (and_6_out, x1, ~q1, ~q3);  // AND_Gate
  and and_7 (and_7_out, ~x1, q1, q2);  // AND_Gate
  and and_8 (and_8_out, ~q1, q2, ~q3);  // AND_Gate
  and and_9 (and_9_out, ~x1, ~x2, ~q1, ~q2, q3);  // AND_Gate
  and and_10 (and_10_out, x1, q3);
  and and_11 (and_11_out, x2, ~q1, ~q2, q3);  // AND_Gate
  and and_12 (and_12_out, ~x1, ~x2, ~q1, q2);  // AND_Gate
  and and_13 (and_13_out, ~x1, ~x2, ~q2, ~q3);  // AND_Gate
  and u_i1 (i1, x2, ~q1, ~q2, q3);  // AND_Gate
  and u_i2 (i2, x2, ~q1, q2, ~q3);  // AND_Gate
  and i4 (i3, x1, q1, ~q2, ~q3);  // AND_Gate
  or u_Q1 (Q1_2, and_1_out, and_2_out, and_3_out, and_4_out);
  or u_Q2 (Q2_2, and_5_out, and_6_out, and_7_out, and_8_out, and_9_out);
  or u_Q3 (Q3_2, and_10_out, and_11_out, and_12_out, and_13_out);

  // Notes on the sheet:
  //   ab 10
  //   x1
  //   x2
  //   x1
  //   x2
  //   q1
  //   q2
  //   q3
  //   q1
  //   q2
  //   q3
endmodule

module memory (
  input  s,
  input  q1,
  input  q2,
  input  q3,
  output q1_2,
  output q1_3,
  output q3_2
);

  wire not_1_out;

  not not_1 (not_1_out, s);
  D_Flip_Flop d_ff_1 (.clk(not_1_out), .D(q1), .Q(q1_2));  // open: Qn, preset, en, reset
  D_Flip_Flop d_ff_2 (.clk(not_1_out), .D(q2), .Q(q1_3));  // open: Qn, preset, en, reset
  D_Flip_Flop d_ff_3 (.clk(not_1_out), .D(q3), .Q(q3_2));  // open: Qn, preset, en, reset
endmodule

module FL (
  input  q1,
  input  q2,
  input  q3,
  output L1,
  output L2,
  output L3,
  output L4,
  output L5,
  output L6
);

  wire and_1_out, and_2_out, and_3_out, and_4_out, and_5_out;

  and and_1 (and_1_out, ~q1, q3);  // AND_Gate
  and and_2 (and_2_out, ~q1, ~q2);  // AND_Gate
  and and_3 (and_3_out, ~q1, q2);  // AND_Gate
  and and_4 (and_4_out, ~q1, ~q3);  // AND_Gate
  and and_5 (and_5_out, ~q2, ~q3);  // AND_Gate
  or or_1 (L1, and_1_out, and_2_out);
  or or_2 (L2, and_3_out, and_4_out);
  and and_6 (L3, q1, ~q2);  // AND_Gate
  or or_3 (L5, q1, and_5_out);
  and and_7 (L6, q1, q3);

  assign L4 = L3;
endmodule

// b.c.
module button_converter (
  input  a,
  input  b,
  input  ab,
  output x1,
  output x2,
  output s
);

  or or_1 (s, a, b, ab);
  and and_1 (x1, ~a, ab);  // AND_Gate

  assign x2 = b;
endmodule

module state_machine (
  input  x1,
  input  x2,
  input  s,
  output i1,
  output i2,
  output i3,
  output L1,
  output L2,
  output L3,
  output L4,
  output L5,
  output L6
);

  wire f_1_q1_2, f_1_q2_2, f_1_q3_2, memory_1_q1_2, memory_1_q1_3, memory_1_q3_2;

  F f_1 (
    .q1(memory_1_q1_2), .q2(memory_1_q1_3), .q3(memory_1_q3_2), .x1(x1), .x2(x2), .Q1_2(f_1_q1_2),
    .Q2_2(f_1_q2_2), .Q3_2(f_1_q3_2), .i1(i1), .i2(i2), .i3(i3));
  memory memory_1 (
    .q1(f_1_q1_2), .q2(f_1_q2_2), .q3(f_1_q3_2), .s(s), .q1_2(memory_1_q1_2), .q1_3(memory_1_q1_3),
    .q3_2(memory_1_q3_2));
  FL fl_1 (
    .q1(memory_1_q1_2), .q2(memory_1_q1_3), .q3(memory_1_q3_2), .L1(L1), .L2(L2), .L3(L3), .L4(L4), .L5(L5),
    .L6(L6));

  // Notes on the sheet:
  //   ab 1 0
endmodule

module clock (
  input  L5,
  input  generator,
  input  i1_signal,
  input  i2_signal,
  input  L6,
  output [3:0] hours_tens,
  output [3:0] hours_units,
  output [3:0] minutes_tens,
  output [3:0] minutes_units,
  output [3:0] sec_tens,
  output [3:0] sec_units
);

  wire and_1_out, and_2_out, and_3_out, and_4_out, and_5_out, and_6_out, controlled_buffer_1_out, or_1_out,
       or_2_out, or_3_out;

  Counter #(.width(4), .max('hf)) counter_1 (
    .Q(hours_tens), .clk(or_2_out), .clr(and_1_out));  // open: load, D, count, carry
  Counter #(.width(4), .max('hf)) counter_2 (
    .Q(hours_units), .clk(or_1_out), .clr(or_2_out));  // open: load, D, count, carry
  or or_1 (or_1_out, and_3_out, i2_signal);
  and and_1 (and_1_out, hours_tens[1], hours_units[2]);
  and and_2 (and_2_out, hours_units[1], hours_units[3]);
  or or_2 (or_2_out, and_2_out, and_1_out);
  Counter #(.width(4), .max('h9)) counter_3 (
    .Q(minutes_tens), .clk(and_4_out), .clr(and_3_out));  // open: load, D, count, carry
  Counter #(.width(4), .max('hf)) counter_4 (
    .Q(minutes_units), .clk(or_3_out), .clr(and_4_out));  // open: load, D, count, carry
  or or_3 (or_3_out, and_5_out, i1_signal);
  and and_3 (and_3_out, minutes_tens[2], minutes_tens[1]);
  and and_4 (and_4_out, minutes_units[3], minutes_units[1]);
  Counter #(.width(4), .max('h9)) counter_5 (
    .Q(sec_tens), .clk(and_6_out), .clr(and_5_out));  // open: load, D, count, carry
  Counter #(.width(4), .max('hf)) counter_6 (
    .Q(sec_units), .clk(controlled_buffer_1_out), .clr(and_6_out));  // open: load, D, count, carry
  assign controlled_buffer_1_out = L5 ? generator : 1'bz;  // Controlled_Buffer controlled_buffer_1
  and and_5 (and_5_out, sec_tens[2], sec_tens[1]);
  and and_6 (and_6_out, sec_units[3], sec_units[1]);

  // Other names for the same wires on the sheet: gen = generator; i1 = i1_signal; i2 = i2_signal
endmodule

module stop_watch (
  input  L5,
  input  generator,
  input  i3_signal,
  input  L6,
  output [3:0] minutes_tens,
  output [3:0] minutes_units,
  output [3:0] sec_tens,
  output [3:0] sec_units
);

  wire and_1_out, and_2_out, and_3_out, and_4_out, controlled_buffer_1_out, or_1_out, or_2_out, or_3_out,
       or_4_out;

  Counter #(.width(4), .max('h9)) counter_1 (
    .Q(minutes_tens), .clk(or_2_out), .clr(or_1_out));  // open: load, D, count, carry
  or or_1 (or_1_out, and_1_out, i3_signal);
  Counter #(.width(4), .max('hf)) counter_2 (
    .Q(minutes_units), .clk(or_3_out), .clr(or_2_out));  // open: load, D, count, carry
  or or_2 (or_2_out, and_2_out, i3_signal);
  and and_1 (and_1_out, minutes_tens[3], minutes_tens[1]);
  and and_2 (and_2_out, minutes_units[3], minutes_units[1]);
  Counter #(.width(4), .max('h9)) counter_3 (
    .Q(sec_tens), .clk(or_4_out), .clr(or_3_out));  // open: load, D, count, carry
  Counter #(.width(4), .max('hf)) counter_4 (
    .Q(sec_units), .clk(controlled_buffer_1_out), .clr(or_4_out));  // open: load, D, count, carry
  assign controlled_buffer_1_out = L6 ? generator : 1'bz;  // Controlled_Buffer controlled_buffer_1
  or or_3 (or_3_out, and_3_out, i3_signal);
  or or_4 (or_4_out, and_4_out, i3_signal);
  and and_3 (and_3_out, sec_tens[2], sec_tens[1]);
  and and_4 (and_4_out, sec_units[3], sec_units[1]);

  // Other names for the same wires on the sheet: gen = generator; i3 = i3_signal
endmodule

module signal (
  input  [3:0] tens,
  input  [3:0] units,
  input  in_3,
  output signal
);

  wire _0_2_out, _00_out, _0_out, _1_out, _3_2_out, _3_out, _5_out, _15_out, _30_out, _45_out,
       controlled_buffer_1_out, counter_1_q, or_1_out;

  and _0 (_0_out, ~tens[3], ~tens[2], ~tens[1], ~tens[0]);  // AND_Gate
  and _1 (_1_out, tens[0], ~tens[1], ~tens[2], ~tens[3]);  // AND_Gate
  and _3 (_3_out, ~tens[3], tens[1], tens[0], ~tens[2]);  // AND_Gate
  and _3_2 (_3_2_out, ~tens[0], ~tens[1], ~tens[3], tens[2]);  // AND_Gate
  and _00 (_00_out, _0_out, _0_2_out);
  and _15 (_15_out, _1_out, _5_out);
  or or_1 (or_1_out, _00_out, _15_out, _30_out, _45_out);
  and _30 (_30_out, _3_out, _0_2_out);
  D_Flip_Flop d_ff_1 (.clk(or_1_out), .D(1'b1), .Q(signal), .reset(counter_1_q));  // open: Qn, preset, en
  and _45 (_45_out, _3_2_out, _5_out);
  assign controlled_buffer_1_out = signal ? in_3 : 1'bz;  // Controlled_Buffer controlled_buffer_1
  and _0_2 (_0_2_out, ~units[3], ~units[2], ~units[1], ~units[0]);  // AND_Gate
  and _5 (_5_out, ~units[3], units[2], units[0], ~units[1]);  // AND_Gate
  Counter #(.width(1), .max('h1)) counter_1 (
    .Q(counter_1_q), .clk(controlled_buffer_1_out), .clr(counter_1_q));  // open: load, D, count, carry

  // Other names for the same wires on the sheet: gen = in_3; minutes_tens[3:0] = tens; minutes_units[3:0] = units
endmodule
